// Logisim project nand2tetris.circ as structural Verilog
module HackALU (
  input  zx,
  input  zy,
  input  nx,
  input  ny,
  input  f,
  input  no,
  input  [15:0] x,
  input  [15:0] y,
  output [15:0] outp,
  output ng,
  output zr
);

  wire or_1_out, or_2_out;
  wire [15:0] adder_1_out, and_1_out, multiplexer_1_out, multiplexer_2_out, multiplexer_3_out,
       multiplexer_4_out, multiplexer_5_out, not_1_out, not_2_out, not_3_out;

  Multiplexer #(.width(16)) multiplexer_1 (.in0(x), .in1({16{1'b0}}), .out(multiplexer_1_out), .sel(zx));
  Multiplexer #(.width(16)) multiplexer_2 (.in0(y), .in1({16{1'b0}}), .out(multiplexer_2_out), .sel(zy));
  assign not_1_out = ~multiplexer_1_out;  // NOT_Gate not_1, 16 bits wide
  assign not_2_out = ~multiplexer_2_out;  // NOT_Gate not_2, 16 bits wide
  Multiplexer #(.width(16)) multiplexer_3 (.in0(multiplexer_1_out), .in1(not_1_out), .out(multiplexer_3_out), .sel(nx));
  Multiplexer #(.width(16)) multiplexer_4 (.in0(multiplexer_2_out), .in1(not_2_out), .out(multiplexer_4_out), .sel(ny));
  assign and_1_out = multiplexer_3_out & multiplexer_4_out;  // AND_Gate and_1, 16 bits wide
  Adder #(.width(16)) adder_1 (.a(multiplexer_3_out), .b(multiplexer_4_out), .out(adder_1_out));  // open: cin, cout
  Multiplexer #(.width(16)) multiplexer_5 (.in0(and_1_out), .in1(adder_1_out), .out(multiplexer_5_out), .sel(f));
  or or_1 (or_1_out, outp[8], outp[9], outp[10], outp[11], outp[12], outp[13], outp[14], ng);
  Multiplexer #(.width(16)) multiplexer_6 (.in0(multiplexer_5_out), .in1(not_3_out), .out({ng, outp[14:0]}), .sel(no));
  assign not_3_out = ~multiplexer_5_out;  // NOT_Gate not_3, 16 bits wide
  or or_2 (or_2_out, outp[0], outp[1], outp[2], outp[3], outp[4], outp[5], outp[6], outp[7]);
  or or_3 (zr, or_2_out, or_1_out);

  assign outp[15] = ng;
endmodule

module OneBitRegister (
  input  inp,
  input  load,
  input  clock,
  output outp
);

  wire multiplexer_1_out;

  Multiplexer multiplexer_1 (.in0(outp), .in1(inp), .out(multiplexer_1_out), .sel(load));
  D_Flip_Flop d_ff_1 (.D(multiplexer_1_out), .clk(clock), .Q(outp));  // open: Qn, preset, reset
endmodule

module SixteenBitRegister (
  input  load,
  input  clock,
  input  [15:0] in_3,
  output [15:0] out_4
);

  OneBitRegister onebitregister_1 (.inp(in_3[0]), .load(load), .clock(clock), .outp(out_4[0]));
  OneBitRegister onebitregister_2 (.inp(in_3[1]), .load(load), .clock(clock), .outp(out_4[1]));
  OneBitRegister onebitregister_3 (.inp(in_3[2]), .load(load), .clock(clock), .outp(out_4[2]));
  OneBitRegister onebitregister_4 (.inp(in_3[3]), .load(load), .clock(clock), .outp(out_4[3]));
  OneBitRegister onebitregister_5 (.inp(in_3[4]), .load(load), .clock(clock), .outp(out_4[4]));
  OneBitRegister onebitregister_6 (.inp(in_3[5]), .load(load), .clock(clock), .outp(out_4[5]));
  OneBitRegister onebitregister_7 (.inp(in_3[6]), .load(load), .clock(clock), .outp(out_4[6]));
  OneBitRegister onebitregister_8 (.inp(in_3[7]), .load(load), .clock(clock), .outp(out_4[7]));
  OneBitRegister onebitregister_9 (.inp(in_3[8]), .load(load), .clock(clock), .outp(out_4[8]));
  OneBitRegister onebitregister_10 (.inp(in_3[9]), .load(load), .clock(clock), .outp(out_4[9]));
  OneBitRegister onebitregister_11 (.inp(in_3[10]), .load(load), .clock(clock), .outp(out_4[10]));
  OneBitRegister onebitregister_12 (.inp(in_3[11]), .load(load), .clock(clock), .outp(out_4[11]));
  OneBitRegister onebitregister_13 (.inp(in_3[12]), .load(load), .clock(clock), .outp(out_4[12]));
  OneBitRegister onebitregister_14 (.inp(in_3[13]), .load(load), .clock(clock), .outp(out_4[13]));
  OneBitRegister onebitregister_15 (.inp(in_3[14]), .load(load), .clock(clock), .outp(out_4[14]));
  OneBitRegister onebitregister_16 (.inp(in_3[15]), .load(load), .clock(clock), .outp(out_4[15]));
endmodule

module RAM8 (
  input  clock,
  input  [15:0] in_2,
  input  [2:0] address,
  input  load,
  output [15:0] outp
);

  wire demultiplexer_2_out0, demultiplexer_2_out1, demultiplexer_2_out2, demultiplexer_2_out3,
       demultiplexer_2_out4, demultiplexer_2_out5, demultiplexer_2_out6, demultiplexer_2_out7;
  wire [15:0] demultiplexer_1_out0, demultiplexer_1_out1, demultiplexer_1_out2, demultiplexer_1_out3,
       demultiplexer_1_out4, demultiplexer_1_out5, demultiplexer_1_out6, demultiplexer_1_out7,
       sixteenbitregister_1_out_4, sixteenbitregister_2_out_4, sixteenbitregister_3_out_4,
       sixteenbitregister_4_out_4, sixteenbitregister_5_out_4, sixteenbitregister_6_out_4,
       sixteenbitregister_7_out_4, sixteenbitregister_8_out_4;

  Demultiplexer #(.select(3), .width(16)) demultiplexer_1 (
    .out0(demultiplexer_1_out0), .out1(demultiplexer_1_out1), .out2(demultiplexer_1_out2),
    .out3(demultiplexer_1_out3), .out4(demultiplexer_1_out4), .out5(demultiplexer_1_out5),
    .out6(demultiplexer_1_out6), .out7(demultiplexer_1_out7), .in(in_2), .sel(address));
  Demultiplexer #(.select(3)) demultiplexer_2 (
    .out0(demultiplexer_2_out0), .out1(demultiplexer_2_out1), .out2(demultiplexer_2_out2),
    .out3(demultiplexer_2_out3), .out4(demultiplexer_2_out4), .out5(demultiplexer_2_out5),
    .out6(demultiplexer_2_out6), .out7(demultiplexer_2_out7), .in(load), .sel(address));
  SixteenBitRegister sixteenbitregister_1 (
    .in_3(demultiplexer_1_out0), .load(demultiplexer_2_out0), .clock(clock),
    .out_4(sixteenbitregister_1_out_4));
  SixteenBitRegister sixteenbitregister_2 (
    .in_3(demultiplexer_1_out1), .load(demultiplexer_2_out1), .clock(clock),
    .out_4(sixteenbitregister_2_out_4));
  SixteenBitRegister sixteenbitregister_3 (
    .in_3(demultiplexer_1_out2), .load(demultiplexer_2_out2), .clock(clock),
    .out_4(sixteenbitregister_3_out_4));
  SixteenBitRegister sixteenbitregister_4 (
    .in_3(demultiplexer_1_out3), .load(demultiplexer_2_out3), .clock(clock),
    .out_4(sixteenbitregister_4_out_4));
  SixteenBitRegister sixteenbitregister_5 (
    .in_3(demultiplexer_1_out4), .load(demultiplexer_2_out4), .clock(clock),
    .out_4(sixteenbitregister_5_out_4));
  SixteenBitRegister sixteenbitregister_6 (
    .in_3(demultiplexer_1_out5), .load(demultiplexer_2_out5), .clock(clock),
    .out_4(sixteenbitregister_6_out_4));
  SixteenBitRegister sixteenbitregister_7 (
    .in_3(demultiplexer_1_out6), .load(demultiplexer_2_out6), .clock(clock),
    .out_4(sixteenbitregister_7_out_4));
  SixteenBitRegister sixteenbitregister_8 (
    .in_3(demultiplexer_1_out7), .load(demultiplexer_2_out7), .clock(clock),
    .out_4(sixteenbitregister_8_out_4));
  Multiplexer #(.select(3), .width(16)) multiplexer_1 (
    .in0(sixteenbitregister_1_out_4), .in1(sixteenbitregister_2_out_4), .in2(sixteenbitregister_3_out_4),
    .in3(sixteenbitregister_4_out_4), .in4(sixteenbitregister_5_out_4), .in5(sixteenbitregister_6_out_4),
    .in6(sixteenbitregister_7_out_4), .in7(sixteenbitregister_8_out_4), .out(outp), .sel(address));
endmodule

module RAM64 (
  input  clock,
  input  [15:0] in_2,
  input  [5:0] address,
  input  load,
  output [15:0] out_5
);

  RAM8 ram8_1 (.clock(clock));  // open: in_2, address, load, outp
  RAM8 ram8_2 (.clock(clock));  // open: in_2, address, load, outp
  RAM8 ram8_3 (.clock(clock));  // open: in_2, address, load, outp
  RAM8 ram8_4 (.clock(clock));  // open: in_2, address, load, outp
  RAM8 ram8_5 (.clock(clock));  // open: in_2, address, load, outp
  RAM8 ram8_6 (.clock(clock));  // open: in_2, address, load, outp
  RAM8 ram8_7 (.clock(clock));  // open: in_2, address, load, outp
  RAM8 ram8_8 (.clock(clock));  // open: in_2, address, load, outp
endmodule
